# Fritzing sketch system_schematic (saved by Fritzing 0.9.3b)
breadboards: 1

parts:
  FR = KY-026 Flame Sensor Module [package="Breakout board"]
  Right = L298N DC motor driver
  Part1 = Arduino Mega ADK (Rev3)
  Front = hc-sr04
  Back = hc-sr04
  FL = KY-026 Flame Sensor Module [package="Breakout board"]
  BR = KY-026 Flame Sensor Module [package="Breakout board"]
  BL = KY-026 Flame Sensor Module [package="Breakout board"]
  RF = DC Motor
  RB = DC Motor
  Left = L298N DC motor driver
  LF = DC Motor
  LB = DC Motor
  12V_||_2100mA = LIPO-1000mAh [package=lipo-1000]
  12V_||_2100mA_2 = LIPO-1000mAh [package=lipo-1000]

nets:
  GND: FR.G, Right.GND, Part1.GND, Front.GND, Back.GND, FL.G, BR.G, BL.G, 12V_||_2100mA_2.-
  5V: FR.+, Part1.5V, Front.VCC, Back.VCC, FL.+, BR.+, BL.+, Left.5V
  N1: FR.D0, Part1.D22
  N2: Right.OUT1, RF.pin_2
  N3: Right.OUT2, RF.pin_1
  N4: Right.OUT3, RB.pin_2
  N5: Right.OUT4, RB.pin_1
  N6: Right.12V, 12V_||_2100mA_2.+
  N7: Right.ENA, Part1.D10_PWM
  N8: Right.IN1, Part1.D2_PWM
  N9: Right.IN2, Part1.D3_PWM
  N10: Right.IN3, Part1.D4_PWM
  N11: Right.IN4, Part1.D5_PWM
  N12: Part1.D11_PWM, Left.ENA
  N13: Part1.D9_PWM, Left.IN4
  N14: Part1.D8_PWM, Left.IN3
  N15: Part1.D6_PWM, Left.IN1
  N16: Part1.D7_PWM, Left.IN2
  N17: Part1.D23, FL.D0
  N18: Part1.D24, BR.D0
  N19: Part1.D25, BL.D0
  N20: Part1.D26, Front.Trig
  N21: Part1.D27, Front.Echo
  N22: Part1.D28, Back.Echo
  N23: Part1.D29, Back.Trig
  N24: Left.OUT1, LF.pin_2
  N25: Left.OUT2, LF.pin_1
  N26: Left.OUT3, LB.pin_2
  N27: Left.OUT4, LB.pin_1
  N28: Left.12V, 12V_||_2100mA.+
  N29: Left.GND, 12V_||_2100mA.-

custom parts:
  KY-026 Flame Sensor Module: KY-026 Flame Sensor Module reacts in the presence of fire.
  L298N DC motor driver: 2x DC motor driver with 78M05 positive voltage regulator (7..35 V) L298N: max 46 V, 2 A Set 5 V Enable jumper to enable 5 V regultor (needed for the L298N) and +5 V output at screw terminal or supply external +5 V at screw terminal Set ENA and/or ENB to +5 V to enable motor permanently or supply ENA and/or ENB with PWM signal IN1 and IN2 set rotation directory for motor A (OUT1/OUT2) IN2 and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
